# Fritzing sketch the_tank (saved by Fritzing 0.9.3b)

parts:
  Arduino_Uno_Rev3 = Arduino Uno (Rev3)
  Arduino_Motorshield_Rev3 = Arduino Motor Shield (Rev3)
  6_VDC_Dual_axis_gear_motors = DC Motor
  M2 = DC Motor
  SBus = JST-B3P-VH [part_number=JST-B3P-VH package=THT]
  FrSky_receiver_e_g_XR8 = JST-B3P-VH [part_number=JST-B3P-VH package=THT]  # not connected
  S_Port = JST-B3P-VH [part_number=JST-B3P-VH package=THT]
  BUC_converter = RioRand LM2596
  LiPo_battery_I_NEED_THE_MARKINGS = LIPO-2000mAh [package=lipo-2000]

nets:
  N1: Arduino_Uno_Rev3.D10_PWM/SS, S_Port.pin1
  N2: Arduino_Uno_Rev3.D11_PWM/MOSI, Arduino_Motorshield_Rev3.D11_PWM/B
  N3: Arduino_Uno_Rev3.D12/MISO, Arduino_Motorshield_Rev3.D12/DirA
  N4: Arduino_Uno_Rev3.D13/SCK, Arduino_Motorshield_Rev3.D13/DirB
  N5: Arduino_Uno_Rev3.D2, Arduino_Motorshield_Rev3.D2
  N6: Arduino_Uno_Rev3.D3_PWM, Arduino_Motorshield_Rev3.D3_PWM/A
  N7: Arduino_Uno_Rev3.D4, Arduino_Motorshield_Rev3.D4
  N8: Arduino_Motorshield_Rev3.B-, 6_VDC_Dual_axis_gear_motors.pin_2
  N9: Arduino_Motorshield_Rev3.B+, 6_VDC_Dual_axis_gear_motors.pin_1
  N10: Arduino_Motorshield_Rev3.A-, M2.pin_2
  N11: Arduino_Motorshield_Rev3.A+, M2.pin_1
  N12: Arduino_Motorshield_Rev3.VMOT, BUC_converter.Pin_3
  N13: Arduino_Motorshield_Rev3.GND, BUC_converter.Pin_4
  N14: Arduino_Motorshield_Rev3.5V, SBus.pin1
  N15: BUC_converter.Pin_1, LiPo_battery_I_NEED_THE_MARKINGS.-
  N16: BUC_converter.Pin_2, LiPo_battery_I_NEED_THE_MARKINGS.+

custom parts:
  LIPO-2000mAh: 2000mAh Lipo-battery
